# Fritzing sketch recover (saved by Fritzing 0.9.3b)
breadboards: 2

parts:
  Part1 = RFID-RC522-v3
  Part2 = Arduino Nano (Rev3.0)
  LCD1 = LCD screen
  LCM1602_IIC1 = LCM1602 IIC [part_number="LCM1602 IIC" chip_label="LCM1602 IIC" package="DIP (Dual Inline) [THT]"]
  R1 = Resistor [tolerance=±5% resistance=330 package=THT]
  LED1 = LED - 5mm [color="Red (633nm)" package="5 mm [THT]"]
  R2 = Resistor [tolerance=±5% resistance=330 package=THT]
  LED2 = LED - 5mm [color="Green (570nm)" package="5 mm [THT]"]
  S1 = Toggle Switch [package=THT]
  R3 = Resistor [tolerance=±5% resistance=1k package=THT]
  R4 = Resistor [tolerance=±5% resistance=1k package=THT]
  U1 = Optocoupler [package=THT]
  TRS2 = Audio Jack (TRS) 3.5mm [package="4Ucon 08780 [THT]"]
  R5 = Resistor [tolerance=±5% resistance=1k package=THT]
  Q1 = NPN-Transistor [package="TO92 [THT]"]
  R6 = Resistor [tolerance=±5% resistance=220 package=THT]
  K1 = Relay [part_number=FRS1B-S package=THT]
  D1 = Rectifier Diode [part_number=1N4001 package="300 mil [THT]"]
  R7 = Resistor [tolerance=±5% resistance=10k package=THT]
  TRS3 = Audio Jack (TRS) 3.5mm [package="4Ucon 08780 [THT]"]

nets:
  N1: Part1.SDA, Part2.D10
  N2: Part1.SCK, Part2.D13/SCK
  N3: Part1.MOSI, Part2.D11/MOSI
  N4: Part1.MISO, Part2.D12/MISO
  GND: Part1.GND, Part2.GND, LCM1602_IIC1.GND, R1.Pin_1, R2.Pin_1, R4.Pin_1, U1.Pin_2, Q1.C, R7.Pin_1
  N5: Part1.RST, Part2.D9
  3.3V: Part1.3.3V, Part2.3V3
  N6: Part2.D2, LED1.anode
  N7: Part2.D3, LED2.anode
  N8: Part2.D4, S1.COM, R4.Pin_0
  5V: Part2.5V, LCM1602_IIC1.VCC, R3.Pin_1, U1.Pin_5, K1.COIL2, D1.cathode
  N9: Part2.A5, LCM1602_IIC1.SCL
  N10: Part2.A4, LCM1602_IIC1.SDA
  VSS: LCD1.VSS, LCM1602_IIC1.VSS
  VDD: LCD1.VDD, LCM1602_IIC1.VDD
  N11: LCD1.V0, LCM1602_IIC1.V0
  N12: LCD1.RS, LCM1602_IIC1.RS
  N13: LCD1.R/W, LCM1602_IIC1.RW
  N14: LCD1.E, LCM1602_IIC1.E
  N15: LCD1.DB0, LCM1602_IIC1.D0
  N16: LCD1.DB1, LCM1602_IIC1.D1
  N17: LCD1.DB2, LCM1602_IIC1.D2
  N18: LCD1.DB3, LCM1602_IIC1.D3
  N19: LCD1.DB4, LCM1602_IIC1.D4
  N20: LCD1.DB5, LCM1602_IIC1.D5
  N21: LCD1.DB6, LCM1602_IIC1.D6
  N22: LCD1.DB7, LCM1602_IIC1.D7
  N23: LCD1.LED+, LCM1602_IIC1.A
  N24: LCD1.LED-, LCM1602_IIC1.K
  N25: LCM1602_IIC1.LED_A, LCM1602_IIC1.LED_B
  N26: R1.Pin_0, LED1.cathode
  N27: R2.Pin_0, LED2.cathode
  N28: S1.L1, R3.Pin_0
  N29: U1.Pin_1, R5.Pin_0
  N30: U1.Pin_4, R6.Pin_1
  N31: TRS2.Ring, TRS2.Tip, K1.B
  N32: Q1.E, K1.COIL1, D1.anode
  N33: Q1.B, R6.Pin_0, R7.Pin_0
  N34: K1.C1, TRS3.Ring, TRS3.Tip

notes:
  3.3V Power Lines
  5V Power Lines

custom parts:
  RFID-RC522-v3: A simple China made RFID-RC522 Reader (6x4 cm); do check the pin labels, as this is a MFRC522 based clone.
  LCM1602 IIC: I2C-Module to use a 1602 or 2004 LCD on with the wire.h libory Serial LCD Modul
