# Fritzing sketch Untitled Sketch (saved by Fritzing 0.9.3b)
breadboards: 1

parts:
  Part1 = RFID-RC522-v3
  Part2 = Arduino Nano (Rev3.0)
  LCD1 = LCD screen  # not connected

nets:
  N1: Part1.SDA, Part2.D10
  N2: Part1.SCK, Part2.D13/SCK
  N3: Part1.MOSI, Part2.D11/MOSI
  N4: Part1.MISO, Part2.D12/MISO
  GND: Part1.GND, Part2.GND
  N5: Part1.RST, Part2.D9
  3.3V: Part1.3.3V, Part2.3V3

notes:
  3.3V Power Lines
  5V Power Lines

custom parts:
  RFID-RC522-v3: A simple China made RFID-RC522 Reader (6x4 cm); do check the pin labels, as this is a MFRC522 based clone.
